# Fritzing sketch Sketch (saved by Fritzing 0.9.3b)
breadboards: 1

parts:
  S2 = Momentary Switch [package=tactile-pth]
  S3 = Momentary Switch [package=tactile-pth]
  PWM1 = PCA9685 16x12-bit PWM Breakout
  J1 = Basic Servo
  VCC1 = 4 x AAA Battery Mount
  MH-ET_LIVE_ESP32_DEVKIT1 = MH-ET LIVE ESP32 DEVKIT 38 pins
  S4 = Momentary Switch [package=tactile-pth]

nets:
  N1: S2.1, S3.1, PWM1.no_name_yet#505, MH-ET_LIVE_ESP32_DEVKIT1.3V3, S4.1
  N2: S2.3, MH-ET_LIVE_ESP32_DEVKIT1.IO32
  N3: S3.3, MH-ET_LIVE_ESP32_DEVKIT1.IO33
  N4: PWM1.no_name_yet#0, J1.pulse
  N5: PWM1.no_name_yet#100, PWM1.no_name_yet#706, J1.vcc, VCC1.+
  N6: PWM1.no_name_yet#501, PWM1.no_name_yet#701, PWM1.no_name_yet#1000, J1.gnd, VCC1.-, MH-ET_LIVE_ESP32_DEVKIT1.GND#70
  N7: PWM1.no_name_yet#503, MH-ET_LIVE_ESP32_DEVKIT1.IO22
  N8: PWM1.no_name_yet#504, MH-ET_LIVE_ESP32_DEVKIT1.IO21
  N9: MH-ET_LIVE_ESP32_DEVKIT1.IO25, S4.3

notes:
  DEC
  INC
  ACK

custom parts:
  MH-ET LIVE ESP32 DEVKIT 38 pins: http://mh.nodebb.com/topic/2/mh-et-live-esp32-devkit
